# Fritzing sketch button_separated (saved by Fritzing 0.9.4)
stripboards: 1

parts:
  S2 = Pushbutton [package="[THT]"]
  S3 = Pushbutton [package="[THT]"]
  S4 = Pushbutton [package="[THT]"]
  S5 = Pushbutton [package="[THT]"]
  S6 = Pushbutton [package="[THT]"]
  S8 = Pushbutton [package="[THT]"]
  S9 = Pushbutton [package="[THT]"]
  S10 = Pushbutton [package="[THT]"]
  S11 = Pushbutton [package="[THT]"]  # not connected
  S1 = Pushbutton [package="[THT]"]
  S12 = Pushbutton [package="[THT]"]
  S13 = Pushbutton [package="[THT]"]
  S14 = Pushbutton [package="[THT]"]
  S15 = Pushbutton [package="[THT]"]
  R3 = Rotary Potentiometer (Small) [maximum_resistance=100kΩ package=THT]
  R4 = Rotary Potentiometer (Small) [maximum_resistance=100kΩ package=THT]
  R5 = Rotary Potentiometer (Small) [maximum_resistance=100kΩ package=THT]
  R6 = Rotary Potentiometer (Small) [maximum_resistance=100kΩ package=THT]

nets:
  N1: S2.Pin_1, S2.Pin_2
  N2: S2.Pin_3, S2.Pin_4, R3.leg2
  N3: S3.Pin_1, S3.Pin_2
  N4: S3.Pin_3, S3.Pin_4, R4.leg2
  N5: S4.Pin_1, S4.Pin_2, R4.leg1
  N6: S4.Pin_3, S4.Pin_4
  N7: S5.Pin_1, S5.Pin_2
  N8: S5.Pin_3, S5.Pin_4, R5.leg2
  N9: S6.Pin_1, S6.Pin_2, R5.leg1
  N10: S6.Pin_3, S6.Pin_4
  N11: S8.Pin_1, S8.Pin_2
  N12: S8.Pin_3, S8.Pin_4
  N13: S9.Pin_1, S9.Pin_2
  N14: S9.Pin_3, S9.Pin_4, R6.leg2
  N15: S10.Pin_1, S10.Pin_2, R6.leg1
  N16: S10.Pin_3, S10.Pin_4
  N17: S1.Pin_1, S1.Pin_2, R3.leg1
  N18: S1.Pin_3, S1.Pin_4
  N19: S12.Pin_1, S12.Pin_2
  N20: S12.Pin_3, S12.Pin_4
  N21: S13.Pin_1, S13.Pin_2
  N22: S13.Pin_3, S13.Pin_4
  N23: S14.Pin_1, S14.Pin_2
  N24: S14.Pin_3, S14.Pin_4
  N25: S15.Pin_1, S15.Pin_2
  N26: S15.Pin_3, S15.Pin_4
